# Fritzing sketch sketch (saved by Fritzing 0.9.9b)
breadboards: 1

parts:
  Part1 = LCD1602-I2C
  R1 = Resistor [tolerance=±5% resistance=130 package="0603 [SMD]"]
  MQ-2 = MQ-2 [package="DIP (Dual Inline) [THT]"]
  MQ-9 = MQ-2 [package="DIP (Dual Inline) [THT]"]
  LED1 = smd LED [color="Blue (470nm)" package="0805 [SMD]"]
  U1 = ESP32S-HiLetgo [part_number=ESP32S-HiLetgo]

nets:
  GND: Part1.GND, MQ-2.pin2, MQ-9.pin2, LED1.anode, U1.GND
  VCC: Part1.VCC, MQ-2.pin1, MQ-9.pin1, U1.VIN
  N1: Part1.SDA, U1.GPIO21
  N2: Part1.SCL, U1.GPIO22
  N3: R1.Pin_0, LED1.cathode
  N4: R1.Pin_1, U1.GPIO32
  N5: MQ-2.pin4, U1.GPIO34
  N6: MQ-9.pin4, U1.GPIO35

custom parts:
  LCD1602-I2C: A standard character display, usually with 2x16 characters. Comes in many colors with LCM1602 IIC attached.
  MQ-2: MQ-2 Gas Sensor module
  ESP32S-HiLetgo: HiLetgo ESP-WROOM-32 ESP32 ESP-32S Development Board 2.4GHz Dual-Mode WiFi + Bluetooth Dual Cores Microcontroller The ESP32 integrated with Antenna switches, RF Balun, power amplifiers, low-noise amplifiers, filters, and management modules, and the entire solution occupies the least area of PCB. 2.4 GHz Wi-Fi plus Bluetooth dual-mode chip, with TSMC Ultra-low power consumption 40nm technology,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
